# Fritzing sketch helotism_powersupply (saved by Fritzing 0.9.0b)
circuit board: 8.46667cm x 5.64444cm
breadboards: 1

parts:
  R5 = Resistor [tolerance=±5% resistance=1k package=THT]
  R6 = Resistor [tolerance=±5% resistance=1k package=THT]
  R3 = Resistor [tolerance=±5% resistance=10k package=THT]
  R4 = Resistor [tolerance=±5% resistance=10k package=THT]
  R1 = Resistor [tolerance=±5% resistance=22k package=THT]
  R2 = Resistor [tolerance=±5% resistance=22k package=THT]
  On = Pushbutton [package="[THT]"]
  S3 = Pushbutton [package="[THT]"]
  Off = Pushbutton [package="[THT]"]
  Q2 = NPN-Transistor [package="TO92 [THT]"]
  Q1 = NPN-Transistor [package="TO92 [THT]"]
  D2 = Rectifier Diode [part_number=1N4001 package="300 mil [THT]"]
  D1 = Rectifier Diode [part_number=1N4001 package="300 mil [THT]"]
  C1 = Electrolytic Capacitor [capacitance=22µF package="100 mil [THT, electrolytic]"]
  LED1 = LED - 5mm [color="Red (633nm)" package="5 mm [THT]"]
  Raspberry_Pi_A1 = Raspberry Pi A
  U1 = RELAY-2 [package=relay-g5v]
  J1_ein = Power Jack [package=power_jack_slot]
  J2 = Power Jack [package=power_jack_slot]

nets:
  N1: R5.Pin_0, Raspberry_Pi_A1.GPIO_4
  N2: R5.Pin_1, R4.Pin_0, S3.Pin_3, S3.Pin_4
  N3: R6.Pin_0, LED1.anode
  N4: R6.Pin_1, S3.Pin_1, S3.Pin_2, D2.anode, Raspberry_Pi_A1.GPIO_14
  N5: R3.Pin_0, Off.Pin_1, Off.Pin_2, Q1.B
  N6: R3.Pin_1, R1.Pin_1, R2.Pin_0, C1.+
  GND: R4.Pin_1, Off.Pin_3, Off.Pin_4, Q2.C, C1.-, LED1.cathode, J1_ein.GND, J2.GND
  N7: R1.Pin_0, U1.1
  N8: R2.Pin_1, D2.cathode
  N9: On.Pin_1, On.Pin_2, D1.cathode, U1.2, U1.10, J2.PWR
  N10: On.Pin_3, On.Pin_4, U1.5, J1_ein.PWR
  N11: Q2.E, Q1.E, D1.anode, U1.9
  N12: Q2.B, Q1.C
